# Fritzing sketch Fritzing Tagger Project (saved by Fritzing 0.9.3b)
circuit board: 6.88566cm x 5.36311cm
breadboards: 1

parts:
  LED_Strip_-_1 = NeoPixel Stick [part_number=1426]
  LED_Strip_-_2 = NeoPixel Stick [part_number=1426]
  Q1 = TRANSISTOR_NPN [package=to-92-ammo]
  LED1 = LEDs [package=led10mm]
  R1_1kΩ = Resistor [tolerance=±5% resistance=1k package=THT]
  R3_100Ω = Resistor [tolerance=±5% resistance=100 package=THT]
  C1_10uf = Tantalum Capacitor [capacitance=10µF package="100 mil [THT, tantalum]"]
  PCB2 = Arduino Shield PCB  # not connected
  LED1_2 = female pin header, 3 pins [form="♀ (female)"]
  LED2 = female pin header, 3 pins [form="♀ (female)"]
  IR = female pin header, 2 pins [form="♀ (female)"]
  SW1 = DIP Switch 8 Position [package=dipswitch-08]
  Part1 = Arduino Uno (Rev3)
  Receiver = female pin header, 3 pins [form="♀ (female)"]
  R2_100Ω = Resistor [tolerance=±5% resistance=100 package=THT]
  IR1 = mystery part, 3 pins [chip_label=?]
  IR2 = mystery part, 3 pins [chip_label=?]
  IR3 = mystery part, 3 pins [chip_label=?]
  IR_RX = female pin header, 3 pins [form="♀ (female)"]

nets:
  +5V: LED_Strip_-_1.+5V, LED_Strip_-_2.+5V, R3_100Ω.Pin_1, LED1_2.pin2, LED2.pin2, Part1.5V, Receiver.pin2, R2_100Ω.Pin_1
  N1: LED_Strip_-_1.DATAIN, LED1_2.pin1, Part1.D6_PWM
  GND: LED_Strip_-_1.GND, LED_Strip_-_2.GND, Q1.C, C1_10uf.-, LED1_2.pin3, LED2.pin3, SW1.11, SW1.12, SW1.13, SW1.14, SW1.15, SW1.16, Part1.GND, Receiver.pin3, IR1.pin2, IR2.pin2, IR3.pin2, IR_RX.pin3
  N2: LED_Strip_-_2.DATAIN, LED2.pin1, Part1.D7
  N3: Q1.E, LED1.C, IR.pin1
  N4: Q1.B, R1_1kΩ.Pin_1
  N5: LED1.A, IR.pin2, R2_100Ω.Pin_0
  N6: R1_1kΩ.Pin_0, Part1.D3_PWM
  N7: R3_100Ω.Pin_0, C1_10uf.+, IR1.pin3, IR2.pin3, IR3.pin3, IR_RX.pin2
  N8: SW1.1, Part1.A0
  N9: SW1.2, Part1.A1
  N10: SW1.3, Part1.A2
  N11: SW1.4, Part1.A3
  N12: SW1.5, Part1.A4/SDA
  N13: SW1.6, Part1.A5/SCL
  N14: Part1.D4, IR1.pin1, IR2.pin1, IR3.pin1, IR_RX.pin1
  N15: Part1.D5_PWM, Receiver.pin1

notes:
  Tagger
  D V+ G
  G V+
  D G V+
  rev1
  Remote IR Receiver Header
  Remote PWM Receiver Header

custom parts:
  NeoPixel Stick: Make your own little LED strip arrangement with this stick of NeoPixel LEDs. We crammed 8 of the tiny 5050 (5mm x 5mm) smart RGB LEDs onto a PCB with mounting holes and a chainable design. Use only one microcontroller pin to control as many as you can chain together! Each LED is addressable as the driver chip is inside the LED. Each one has ~18mA constant current drive so the color will be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
  Arduino Shield PCB: Plain PCB Shaped to fit an Arduino "Shield"
